// Logisim project Demultiplexador.circ as structural Verilog: 1 circuit, main circuit main
module main (
  input  E,
  input  [1:0] C2,
  input  C1,
  input  C2_2,
  input  E_2,
  output D0,
  output D1,
  output D2,
  output D3,
  output D0_2,
  output D1_2,
  output D2_2,
  output D3_2
);

  wire not_1_out, not_2_out;

  not not_1 (not_1_out, C1);
  not not_2 (not_2_out, C2_2);
  Demultiplexer #(.select(2)) demultiplexer_1 (
    .out0(D0), .out1(D1), .out2(D2), .out3(D3), .in(E), .sel(C2));  // open: en
  and and_1 (D0_2, E_2, not_1_out, not_2_out);
  and and_2 (D1_2, not_1_out, C2_2, E_2);
  and and_3 (D2_2, C1, not_2_out, E_2);
  and and_4 (D3_2, C1, C2_2, E_2);

  // Notes on the sheet:
  //   C1
endmodule
